// Logisim project teclaDO.circ as structural Verilog: 2 circuits, main circuit main
module main (
);

  wire _0, _1, _2, _3, _4, _5, _6, _7, _8, _9, b0, b1, b2, b3;

  Button u__7 (.out(_7));
  Button u__8 (.out(_8));
  Button u__4 (.out(_4));
  Button u__5 (.out(_5));
  Button u__2 (.out(_2));
  Button u__1 (.out(_1));
  Button u__0 (.out(_0));
  Button u__9 (.out(_9));
  Button u__6 (.out(_6));
  Button u__3 (.out(_3));
  dectobin dectobin_1 (
    ._0(_0), ._1(_1), ._2(_2), ._3(_3), ._4(_4), ._5(_5), ._6(_6), ._7(_7), ._8(_8), ._9(_9), .b3(b3),
    .b2(b2), .b1(b1), .b0(b0));
  // Probe on b3
  // Probe on b2
  // Probe on b1
  // Probe on b0
endmodule

module dectobin (
  input  _0,
  input  _1,
  input  _2,
  input  _3,
  input  _4,
  input  _5,
  input  _6,
  input  _7,
  input  _8,
  input  _9,
  output b3,
  output b2,
  output b1,
  output b0
);

  or or_1 (b3, _8, _9);
  or or_2 (b2, _7, _6, _5, _4);
  or or_3 (b1, _2, _3, _7, _6);
  or or_4 (b0, _1, _3, _5, _7, _9);
endmodule
